// Logisim project third_exp.circ as structural Verilog: 1 circuit, main circuit main
module main (
  input  in_1,
  input  in_2,
  input  in_3,
  input  in_4,
  input  in_5,
  output out_6,
  output out_7,
  output out_8,
  output out_9
);

  wire and_2_out, and_3_out, xor_2_out;

  xor xor_1 (out_6, in_1, in_2);
  and and_1 (out_7, in_1, in_2);
  xor xor_2 (xor_2_out, in_3, in_4);
  and and_2 (and_2_out, in_3, in_4);
  xor xor_3 (out_8, xor_2_out, in_5);
  and and_3 (and_3_out, xor_2_out, in_5);
  or or_1 (out_9, and_3_out, and_2_out);

  // Notes on the sheet:
  //   Half Adder 
  //   full Adder 
  //   Name : Astha
  //   Roll no.2400320100320
  //   Section : CSE15
endmodule
